# Fritzing sketch Leaflift_core_v1 (saved by Fritzing 0.9.3b)
circuit board: 9.14207cm x 4.67733cm
breadboards: 4

parts:
  C1 = Electrolytic Capacitor [capacitance=47µF voltage=16V package="100 mil [THT, electrolytic]"]
  128x64_LCD = OLED 0.96" 128x64 I2C SSD1306  # not connected
  C2 = Ceramic Capacitor [capacitance=10µF voltage=16V package="100 mil [THT, multilayer]"]
  C3 = Electrolytic Capacitor [capacitance=47µF voltage=16V package="100 mil [THT, electrolytic]"]  # not connected
  U2 = RJ45 Jack [package=rj45-8]  # not connected
  JP1 = Header 8 [package=bm08b-srss-tb]  # not connected
  JP2 = Header 4 [package=1x04-1mm-ra]  # not connected
  pH_Circuit = pH Circuit
  Probe_BNC = Pre-Assembled Female BNC
  U3 = RJ45 Jack [package=rj45-8]  # not connected
  U4 = RJ45 Jack [package=rj45-8]  # not connected
  U5 = RJ45 Jack [package=rj45-8]  # not connected
  RHT1 = Humidity and Temperature Sensor RHT03  # not connected
  S1 = Pushbutton [package="[THT]"]  # not connected
  S2 = Toggle Switch [package=THT]  # not connected
  U6 = Voltage Regulator - 5V [package="TO220 [THT]"]  # not connected
  U7 = RJ45 Jack [package=rj45-8]  # not connected
  3 = female pin header, 4 pins [form="♀ (female)"]
  2 = female pin header, 4 pins [form="♀ (female)"]
  1 = female pin header, 4 pins [form="♀ (female)"]
  SCL = Pad [width=1.5051851851851958 height=19.379259259259253 connect=center]  # not connected
  SDA = Pad [width=1.9755555555555555 height=22.107407407407408 connect=center]  # not connected
  A0 = female pin header, 1 pin [form="♀ (female)"]
  Node = NodeMCU V1.0
  10k = Resistor [tolerance=±5% resistance=10k package=THT]
  sx3 = female pin header, 12 pins [form="♀ (female)"]
  sx4 = female pin header, 12 pins [form="♀ (female)"]
  MCP23017 = IC, DIP package, 28 pins [chip_label=MCP23017]
  FTDI1 = female pin header, 6 pins [form="♀ (female)"]  # not connected
  UART1 = female pin header, 4 pins [form="♀ (female)"]  # not connected

nets:
  N1: C1.-, C2.0, pH_Circuit.GND#0, 3.pin2, 2.pin2, 1.pin2, Node.GND, sx3.pin6, sx4.pin6, MCP23017.pin10, MCP23017.pin15, MCP23017.pin16, MCP23017.pin17
  VCC: C1.+, pH_Circuit.Vcc, Probe_BNC.NC, 3.pin1, 2.pin1, 1.pin1, Node.3V3, 10k.Pin_1, sx3.pin5, sx4.pin5, MCP23017.pin9
  N2: C2.1, Node.Vin
  N3: pH_Circuit.TX, 3.pin4, 2.pin4, 1.pin4, Node.D2, sx3.pin12, sx4.pin12, MCP23017.pin12
  N4: pH_Circuit.RX, 3.pin3, 2.pin3, 1.pin3, Node.D1, sx3.pin11, sx4.pin11, MCP23017.pin13
  N5: pH_Circuit.PRB, Probe_BNC.PRB
  N6: pH_Circuit.GND#5, Probe_BNC.GND
  N7: A0.pin1, Node.A0
  N8: 10k.Pin_0, MCP23017.pin18
  N9: sx3.pin1, MCP23017.pin21
  N10: sx3.pin2, MCP23017.pin22
  N11: sx3.pin3, MCP23017.pin23
  N12: sx3.pin4, MCP23017.pin24
  N13: sx3.pin7, MCP23017.pin25
  N14: sx3.pin8, MCP23017.pin26
  N15: sx3.pin9, MCP23017.pin27
  N16: sx3.pin10, MCP23017.pin28
  N17: sx4.pin1, MCP23017.pin8
  N18: sx4.pin2, MCP23017.pin7
  N19: sx4.pin3, MCP23017.pin6
  N20: sx4.pin4, MCP23017.pin5
  N21: sx4.pin7, MCP23017.pin4
  N22: sx4.pin8, MCP23017.pin3
  N23: sx4.pin9, MCP23017.pin2
  N24: sx4.pin10, MCP23017.pin1

notes:
  leaflift v1.0
  SDA | SCL
  SDA
  SCL
  1W
  3V
  GND

custom parts:
  NodeMCU V1.0: ESP9266 based NodeMCU
